# Fritzing sketch thermeq3 (saved by Fritzing 0.9.3b)
breadboards: 1

parts:
  Yun = Arduino Yun
  U1 = RELAY [package=relay-t9a]
  LED2 = RGB LED (com. cathode, rgb) [package="5 mm [THT]"]
  R1 = Resistor [tolerance=±5% resistance=220 package="0805 [SMD]"]
  R2 = Resistor [tolerance=±5% resistance=220 package="0805 [SMD]"]
  R3 = Resistor [tolerance=±5% resistance=220 package="0805 [SMD]"]
  JP1 = Header 2 [package=screwterminal-3.5mm-2_lock]

nets:
  N1: Yun.5V, U1.COIL1
  N2: Yun.D8, R1.Pin_0
  N3: Yun.D9_PWM, R2.Pin_0
  N4: Yun.D10_PWM/SS, U1.COIL2
  N5: Yun.D13/SCK, R3.Pin_0
  N6: Yun.GND, LED2.common_cathode
  N7: U1.MAIN, JP1.1
  N8: U1.NO, JP1.2
  N9: LED2.red_anode, R1.Pin_1
  N10: LED2.green_anode, R3.Pin_1
  N11: LED2.blue_anode, R2.Pin_1
